# Fritzing sketch Humidifier (saved by Fritzing 0.9.3b)
breadboards: 1

parts:
  DHT1 = DHT11 Humitidy and Temperature Sensor
  LCM1602_IIC1 = LCM1602 IIC [part_number="LCM1602 IIC" chip_label="LCM1602 IIC" package="DIP (Dual Inline) [THT]"]
  LCD1 = LCD screen
  Componente1 = Arduino Uno (Rev3) - ICSP
  U1 = POT [package=pot_alpha_rv16af-20]
  Q1 = npn-Powertransistor [package="TO220 [THT]"]
  D1 = Diode [package=diode-1n4148]
  R1 = Resistor [tolerance=±5% resistance=100k package="0603 [SMD]"]
  M1 = DC Motor

nets:
  N1: DHT1.DATA, Componente1.D5_PWM
  GND: DHT1.GND, LCM1602_IIC1.GND, Componente1.GND, U1.E, Q1.emitter
  VSS: LCM1602_IIC1.VSS, LCD1.VSS
  VDD: LCM1602_IIC1.VDD, LCD1.VDD
  N2: LCM1602_IIC1.V0, LCD1.V0
  N3: LCM1602_IIC1.RS, LCD1.RS
  N4: LCM1602_IIC1.RW, LCD1.R/W
  N5: LCM1602_IIC1.E, LCD1.E
  N6: LCM1602_IIC1.D0, LCD1.DB0
  N7: LCM1602_IIC1.D1, LCD1.DB1
  N8: LCM1602_IIC1.D2, LCD1.DB2
  N9: LCM1602_IIC1.D3, LCD1.DB3
  N10: LCM1602_IIC1.D4, LCD1.DB4
  N11: LCM1602_IIC1.D5, LCD1.DB5
  N12: LCM1602_IIC1.D6, LCD1.DB6
  N13: LCM1602_IIC1.D7, LCD1.DB7
  N14: LCM1602_IIC1.A, LCD1.LED+
  N15: LCM1602_IIC1.K, LCD1.LED-
  VCC: LCM1602_IIC1.VCC, Componente1.5V, U1.A
  N16: LCM1602_IIC1.SDA, Componente1.A4/SDA
  N17: LCM1602_IIC1.SCL, Componente1.A5/SCL
  N18: Componente1.A0, U1.S
  N19: Componente1.D2, R1.Pin_0
  N20: Componente1.VIN, M1.pin_2
  N21: Q1.base, R1.Pin_1
  N22: Q1.collector, D1.A, M1.pin_1

custom parts:
  DHT11 Humitidy and Temperature Sensor: DHT11 Humidity and Temperature Sensor
  LCM1602 IIC: I2C-Module to use a 1602 or 2004 LCD on with the wire.h libory Serial LCD Modul
